// Logisim project 1905052.circ as structural Verilog: 1 circuit, main circuit main
module main (
  input  w,
  input  x,
  input  y,
  input  z,
  output out_5
);

  wire n7408_1_p3, n7408_1_p6, n7408_1_p9, n7408_1_p11, n7408_2_p3, n7408_2_p6, n7408_2_p11, n7408_2_p14,
       n7408_3_p3, n74138_1_p9, n74138_1_p10, n74138_1_p11, n74138_2_p13, n74138_2_p16, n74138_2_p17,
       n74138_2_p18, n74138_2_p19, n74138_2_p20, n74138_2_p21;

  // _74138 74138_1: pin names not known; wires that end beside it: 1'b1, z, y, x, w, 1'b0, 1'b1, 1'b1, n74138_1_p9, n74138_1_p10, n74138_1_p11
  // _74138 74138_2: pin names not known; wires that end beside it: w, 1'b0, x, y, z, 1'b0, z, y, x, 1'b0, 1'b0, w, n74138_2_p13, 1'b0, 1'b1, n74138_2_p16, n74138_2_p17, n74138_2_p18, n74138_2_p19, n74138_2_p20, n74138_2_p21
  // _7408 7408_1: pin names not known; wires that end beside it: n74138_1_p9, n74138_1_p10, n7408_1_p3, n7408_1_p3, n74138_1_p11, n7408_1_p6, 1'b0, 1'b1, n7408_1_p9, n74138_2_p17, n7408_1_p11, n7408_1_p6, n74138_2_p16, n7408_1_p9
  // _7408 7408_2: pin names not known; wires that end beside it: n7408_1_p11, n74138_2_p18, n7408_2_p3, n7408_2_p3, n74138_2_p19, n7408_2_p6, 1'b0, 1'b1, n7408_2_p6, n74138_2_p20, n7408_2_p11, n7408_2_p11, n74138_2_p21, n7408_2_p14
  // _7408 7408_3: pin names not known; wires that end beside it: n7408_2_p14, n74138_2_p13, n7408_3_p3, 1'b0, 1'b1
  // _7404 7404_1: pin names not known; wires that end beside it: 1'b0, 1'b1, n7408_3_p3, out_5, 1'b0, 1'b1
endmodule
