// Logisim project 1905052.circ as structural Verilog: 1 circuit, main circuit main
module main (
  input  B,
  input  D,
  input  A,
  input  C,
  output f
);

  wire n7404_1_p3, n7404_1_p5, n7408_1_p3, n7408_1_p6, n7408_1_p11, n7432_1_p3;

  // _7404 7404_1: pin names not known; wires that end beside it: 1'b1, C, n7404_1_p3, A, n7404_1_p5, 1'b0, 1'b1
  // _7408 7408_1: pin names not known; wires that end beside it: A, n7404_1_p3, n7408_1_p3, n7404_1_p5, C, n7408_1_p6, 1'b0, 1'b1, n7404_1_p5, n7404_1_p3, n7408_1_p11
  // _7432 7432_1: pin names not known; wires that end beside it: n7408_1_p6, n7408_1_p3, n7432_1_p3, 1'b0, 1'b1
  // _74153 74153_1: pin names not known; wires that end beside it: n7408_1_p11, n7432_1_p3, 1'b0, B, A, n7408_1_p11, n7432_1_p3, n7404_1_p3, f, 1'b0, 1'b1, D
endmodule
