// Logisim project 1905052.circ as structural Verilog: 3 circuits, main circuit main
module main (
  input  [3:0] X,
  output out_2
);

  wire n7404_1_p2, n7404_1_p4, n7404_1_p6, n7408_2_p3, n7432_1_p1, n7432_1_p2, n7432_1_p3, n7432_1_p6,
       n7432_1_p9, n7432_1_p10;

  // _7404 7404_1: pin names not known; wires that end beside it: X[0], n7404_1_p2, X[1], n7404_1_p4, X[3], n7404_1_p6, 1'b0, 1'b1
  // _7432 7432_1: pin names not known; wires that end beside it: n7432_1_p1, n7432_1_p2, n7432_1_p3, X[1], X[2], n7432_1_p6, 1'b0, 1'b1, n7432_1_p9, n7432_1_p10, out_2
  // _7408 7408_1: pin names not known; wires that end beside it: X[3], n7404_1_p2, n7432_1_p1, X[2], X[0], n7432_1_p2, 1'b1, n7432_1_p3, n7404_1_p4, n7432_1_p10, n7432_1_p6, X[0]
  // _7408 7408_2: pin names not known; wires that end beside it: 1'b0, 1'b0, n7408_2_p3, 1'b1, n7408_2_p3, n7404_1_p6, n7432_1_p9

  // Notes on the sheet:
  //   x1'(x3 x0'+x2 x0)+x3' x0(x2+x1)
endmodule

module step2 (
  input  [3:0] X,
  output F_X,
  output F_X_prime
);

  main main_1 (.X(X), .out_2(F_X));
  // _7404 7404_1: pin names not known; wires that end beside it: F_X, F_X_prime, 1'b0, 1'b1
endmodule

module step3 (
  input  [3:0] A,
  input  [3:0] B,
  output OUTPUT
);

  wire n7408_1_p3, n7408_1_p6, step2_1_f_x, step2_1_f_x_prime, step2_2_f_x, step2_2_f_x_prime;

  step2 step2_1 (.X(A), .F_X(step2_1_f_x), .F_X_prime(step2_1_f_x_prime));
  step2 step2_2 (.X(B), .F_X(step2_2_f_x), .F_X_prime(step2_2_f_x_prime));
  // _7408 7408_1: pin names not known; wires that end beside it: step2_1_f_x, step2_2_f_x_prime, n7408_1_p3, step2_1_f_x_prime, step2_2_f_x, n7408_1_p6, 1'b0, 1'b1
  // _7432 7432_1: pin names not known; wires that end beside it: n7408_1_p3, n7408_1_p6, OUTPUT, 1'b0, 1'b1
endmodule
