// Logisim project 1905052.circ as structural Verilog: 1 circuit, main circuit main
module main (
  output y0,
  output y2,
  output y1
);

  wire clock_1_out, n7408_1_p2, n7408_1_p3, n7408_1_p11, n7408_2_p3, n7408_2_p6, n7408_2_p10, n7408_2_p13,
       n7432_1_p3, n7432_2_p1, n7474_1_p1, n7474_1_p4, n7474_1_p7, n7474_1_p10, n7474_2_p1;

  Clock clock_1 (.out(clock_1_out));
  // _7474 7474_1: pin names not known; wires that end beside it: n7474_1_p1, clock_1_out, y2, n7474_1_p4, 1'b0, 1'b1, n7474_1_p7, clock_1_out, y1, n7474_1_p10
  // _7408 7408_1: pin names not known; wires that end beside it: n7474_1_p10, n7408_1_p2, n7408_1_p3, y1, y0, n7408_1_p3, 1'b0, 1'b1, y1, n7408_1_p2, n7408_1_p11
  // _7408 7408_2: pin names not known; wires that end beside it: n7474_1_p4, y0, n7408_2_p3, n7474_1_p4, n7408_1_p2, n7408_2_p6, 1'b1, n7474_1_p4, n7474_1_p10, n7408_2_p10, y2, y1, n7408_2_p13
  // _7474 7474_2: pin names not known; wires that end beside it: n7474_2_p1, clock_1_out, y0, n7408_1_p2, 1'b0, 1'b1
  // _7432 7432_1: pin names not known; wires that end beside it: n7408_2_p10, n7408_2_p13, n7432_1_p3, n7432_1_p3, n7408_1_p11, n7474_2_p1, 1'b0, 1'b1, 1'b1
  // _7432 7432_2: pin names not known; wires that end beside it: n7432_2_p1, n7432_2_p1, n7408_2_p3, n7474_1_p1, 1'b0, 1'b1, n7408_2_p6, n7474_1_p10, n7474_1_p7, 1'b0
endmodule
